# Fritzing sketch SQArduinoCampingFridgeCircuit (saved by Fritzing 0.9.2b)

parts:
  Part1 = Arduino Uno (Rev3)
  RHT1 = Humidity and Temperature Sensor RHT03
  U1 = DS1307 [package=so08]
  IC1 = ULN2003A [package="SO16 [SMD]"]
  U2 = RELAY-SOLIDSTATE [package=relay-s108t02]
  F1 = FUSE [package=fuse_5mm]

nets:
  N1: Part1.A4/SDA, U1.SDA
  N2: Part1.A5/SCL, U1.SCL
  N3: Part1.D12/MISO, RHT1.Data-signal
  N4: Part1.D13/SCK, IC1.In_1
  5V: Part1.5V, RHT1.Vcc, U1.X2
  GND: Part1.GND, RHT1.GND_2, IC1.0V
  N5: IC1.Out_1, U2.-
  N6: U2.T2, U2.+, F1.1
  12V: F1.2
